# Fritzing sketch clock-pcb (saved by Fritzing 0.9.3b)
circuit board: 13.3229cm x 8.31985cm
breadboards: 4

parts:
  BUZZER = Buzzer 12mm [package=buzzer-12mm-ns-kit]
  Arduino_Nano = Arduino Nano (Rev3.0)
  Y1 = CRYSTAL [part_number=32.768kHz package=tc26h]
  IC2 = DS1302 [package="DIP8 [THT]"]
  R1 = Resistor [tolerance=±5% resistance=47k power=.25W package=THT]
  R2 = Resistor [tolerance=±5% resistance=220 power=0.25W package=THT]
  S1 = Pushbutton [package="[THT]"]
  S2 = Pushbutton [package="[THT]"]
  S3 = Pushbutton [package="[THT]"]
  S4 = Pushbutton [package="[THT]"]
  S8 = Pushbutton [package="[THT]"]
  D1 = LED - 5mm [color="Green (555nm)" package="5 mm [THT]"]
  SWITCH = female pin header, 2 pins [form="♀ (female)"]
  9V = Battery block 9V
  S5 = Pushbutton [package="[THT]"]
  S6 = Pushbutton [package="[THT]"]
  S7 = Pushbutton [package="[THT]"]
  J2 = rounded female pin header, 7 pins [form="♀ (female rounded)"]
  J1 = rounded female pin header, 7 pins [form="♀ (female rounded)"]
  IC1 = MAX7219 [package=dil24]
  R3 = Resistor [tolerance=±5% resistance=220 package=THT]
  BATTERY = Battery Holders [package=battcom_20mm_pth]

nets:
  BUZZER: BUZZER.1, Arduino_Nano.D9
  GND: BUZZER.2, Arduino_Nano.GND, IC2.0V, S1.Pin_1, S1.Pin_2, S2.Pin_1, S2.Pin_2, S3.Pin_1, S3.Pin_2, S4.Pin_1, S4.Pin_2, S8.Pin_1, S8.Pin_2, D1.cathode, 9V.-, S5.Pin_1, S5.Pin_2, S6.Pin_1, S6.Pin_2, S7.Pin_1, S7.Pin_2, J2.pin7, IC1.GND, IC1.GND2, BATTERY.-
  CLK: Arduino_Nano.D2, IC2.SCLK_-_SPI_Clock
  DAT: Arduino_Nano.D3, IC2.I/O_-_SPI_Data_In/Out
  RST: Arduino_Nano.D4, IC2.CE_-_Chip_Enable
  DIN: Arduino_Nano.D5, IC1.DIN
  LOAD: Arduino_Nano.D6, IC1.LOAD
  CLK_LED: Arduino_Nano.D7, IC1.CLK
  N1: Arduino_Nano.D8, R2.Pin_0
  N2: Arduino_Nano.D10, R3.Pin_1
  TIME +: Arduino_Nano.D11/MOSI, S1.Pin_3, S1.Pin_4
  TIME -: Arduino_Nano.D12/MISO, S2.Pin_3, S2.Pin_4
  N3: Arduino_Nano.VIN, SWITCH.pin1
  5V: Arduino_Nano.5V, IC2.+V, R1.Pin_0, IC1.VCC
  N4: Arduino_Nano.A5, S3.Pin_3, S3.Pin_4
  N5: Arduino_Nano.A4, S4.Pin_3, S4.Pin_4
  N6: Arduino_Nano.A3, S8.Pin_3, S8.Pin_4
  N7: Arduino_Nano.A2, S5.Pin_3, S5.Pin_4
  N8: Arduino_Nano.A1, S6.Pin_3, S6.Pin_4
  N9: Arduino_Nano.A0, S7.Pin_3, S7.Pin_4
  N10: Y1.1, IC2.X2_-_Crystal
  N11: Y1.2, IC2.X1_-_Crystal
  N12: IC2.Vbat_-_Backup_Supply, BATTERY.+
  N13: R1.Pin_1, IC1.ISET
  COLON: R2.Pin_1, J1.pin7
  N14: D1.anode, R3.Pin_0
  N15: SWITCH.pin2, 9V.+
  E: J2.pin1, IC1.SEGE
  D: J2.pin2, IC1.SEGD
  DP: J2.pin3, IC1.SEGDP
  C: J2.pin4, IC1.SEGC
  G: J2.pin5, IC1.SEGG
  DIG 3: J2.pin6, IC1.DIG3
  DIG 0: J1.pin1, IC1.DIG0
  A: J1.pin2, IC1.SEGA
  F: J1.pin3, IC1.SEGF
  DIG 1: J1.pin4, IC1.DIG1
  DIG 2: J1.pin5, IC1.DIG2
  B: J1.pin6, IC1.SEGB

notes:
  USB
  1
  Arduino Clock v2
  TIME+       TIME-      ALARM+     ALARM-      SLEEP
  ALARM ON/OFF
  -  +
  SNOOZE
